# Fritzing sketch tom servo (saved by Fritzing 1.0.0rc)
stripboards: 1

parts:
  J1 = Basic Servo
  BATT4 = 4xAA Switchable Battery Pack w/Bare Wire
  Part6 = Arduino Pro Mini (5V)  # not connected
  DFRobot_DFPlayer_Mini3 = DFRobot DFPlayer Mini [part_number=DFR0299]
  R5 = Resistor [tolerance=±5% power=0.25 resistance=1k package=THT]
  R6 = Resistor [tolerance=±5% power=0.25 resistance=1k package=THT]
  U1 = Voltage Regulator - 3.3V [package="TO220 [THT]"]
  S3 = Pushbutton [package="[THT]"]
  C3 = Electrolytic Capacitor [capacitance=1000μF voltage=35V package="1010 [SMD, electrolytic]"]
  SP2 = SPEAKER [package=pcb_mount_speaker]
  SP3 = SPEAKER [package=pcb_mount_speaker]

nets:
  GND: J1.gnd, BATT4.NEG, DFRobot_DFPlayer_Mini3.GND-1, DFRobot_DFPlayer_Mini3.GND-2, U1.GND, S3.Pin_1, S3.Pin_2, C3.+, SP2.+, SP3.+
  N1: J1.vcc, BATT4.POS, U1.input_voltage, C3.-
  N2: DFRobot_DFPlayer_Mini3.VCC, U1.output_voltage
  N3: DFRobot_DFPlayer_Mini3.RX, R6.Pin_0, R6.Pin_1
  N4: DFRobot_DFPlayer_Mini3.TX, R5.Pin_0, R5.Pin_1
  N5: DFRobot_DFPlayer_Mini3.SPK_1, SP2.-
  N6: DFRobot_DFPlayer_Mini3.SPK_2, SP3.-
  N7: S3.Pin_3, S3.Pin_4

custom parts:
  4xAA Switchable Battery Pack w/Bare Wire: 4xAA Switchable Battery Pack with Bare Wire connection
